# Fritzing sketch Wiring (saved by Fritzing 1.0.1rc)
breadboards: 1

parts:
  Teensy_3_2 = Teensy 3.1
  U1 = LIPO-1000mAh [package=lipo-1000]
  M1 = RioRand LM2596
  M2 = Dagu DGServo 9g (Top view) [part_number=RS001B]
  JP1 = Header 3 [package=molex-1x3_lock]
  JP2 = Header 3 [package=molex-1x3_lock]
  A1 = Littlebee 20A ESC

nets:
  GND: Teensy_3_2.GND, U1.-, M1.Pin_2, M1.Pin_4, M2.gnd, JP1.3, A1.Pin_1, A1.Pin_6
  N1: Teensy_3_2.D3, M2.pulse
  N2: Teensy_3_2.D9, A1.Pin_7
  N3: Teensy_3_2.D11, JP1.2
  N4: Teensy_3_2.D12, JP2.1
  N5: Teensy_3_2.D13, JP2.2
  VIN: Teensy_3_2.Vin, M1.Pin_3, M2.vcc, JP1.1
  N6: U1.+, M1.Pin_1, A1.Pin_2

notes:
  Driver motor ESC
  Steering Servo
  Dc to Dc Converter 7.2v -> 5v
  7.2v Battery
  Pixy 2.1 Cable goes like in the drowing on the right
  | |
  | |
  | |
  _|___|_
  |______|

custom parts:
  Littlebee 20A ESC: LittleBee 20A 2-4 LiPo Battery OPTO ESC Brushless Speed Controller for RC FPV Multicopter.
